# Fritzing sketch arugino (saved by Fritzing 0.9.2b)
breadboards: 1

parts:
  Part2 = Arduino Uno (Rev3)
  DIP-Relay2 = DIP-Relay-D31A [part_number=D31A*]
  U4 = SWITCH_SPDT [package=kps-1290]
  M2 = DC Motor
  Power_plug2 = Power plug
  Q3 = NPN-Transistor [package="TO92 [THT]"]
  R7 = Resistor [tolerance=±5% resistance=6.5k package=THT]
  Capacitive_Soil_Moisture_Sensor1 = DFRobot Capacitive Soil Moisture Sensor V1.0 [part_number=SEN0193]
  S1 = Round Pushbutton
  R8 = Resistor [tolerance=±5% resistance=10k package="1206 [SMD]"]

nets:
  N1: Part2.A0, Capacitive_Soil_Moisture_Sensor1.A
  N2: Part2.D13/SCK, DIP-Relay2.COIL1_+
  N3: Part2.D2, S1.leg1, R8.Pin_0
  N4: Part2.5V, U4.P
  GND: Part2.GND, DIP-Relay2.B1_Switch_Terminal_B, Power_plug2.GND, Q3.E, Capacitive_Soil_Moisture_Sensor1.GND, R8.Pin_1
  VIN: Part2.VIN, M2.pin_1, Power_plug2.VCC
  N5: DIP-Relay2.A1_Switch_Terminal_A, M2.pin_2
  N6: DIP-Relay2.Coil2_-, Q3.C
  N7: U4.O, R7.Pin_0, Capacitive_Soil_Moisture_Sensor1.VCC, S1.leg0
  N8: Q3.B, R7.Pin_1

notes:
  NPN base resistor:
  I_c = h_fe*I_b
  I_c ~= 40mA
  h_fe ~= 60
  --> I_b ~= 666uA
  V_be = 0.7V
  V_p13 = 5V
  V_r = 4.3V
  R = V/I = 4.3/666u ~= 6.5k ohm
  TODO:
  1. Sleep / Wake - RTC for pump + Push button for LCD (but how can I save previous pump time without power? EEPROM?)
  2. Move project to a breadboard
  (3. Move main switch outside breadboard)
  Float Switch

custom parts:
  DFRobot Capacitive Soil Moisture Sensor V1.0: DFRobot Capacitive Soil Moisture Sensor V1.0 This product measures soil moisture levels by capacitive sensing, rather than resistive sensing like other types of moisture sensor. It is made of a corrosion resistant material giving it a long service life. Insert it into soil and impress your friends with the real-time soil moisture data! The product includes an on-board voltage regulator which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
